# Fritzing sketch Platine_ESP32TDMX_V1 (saved by Fritzing 1.0.7)
circuit board: 6.61821cm x 5.77781cm
breadboards: 1

parts:
  BUCK_CONVERTER_5V = Mini-360 DC-DC Buck converter [package=THT]
  MAX485 = MAX485 Breakout LB Version [package=THT]
  ESP32 = ESP 32 DEVKIT DOIT
  POWER = screw terminal, 2 pins
  DMX = screw terminal, 4 pins

nets:
  N1: BUCK_CONVERTER_5V.IN-, POWER.pin1
  N2: BUCK_CONVERTER_5V.IN+, POWER.pin2
  N3: BUCK_CONVERTER_5V.OUT+, BUCK_CONVERTER_5V.OUT-, ESP32.VP, ESP32.GND#13, ESP32.Vin#14
  N4: MAX485.RE, MAX485.DE
  N5: MAX485.DI, ESP32.D2
  N6: MAX485.GND, ESP32.GND#16, DMX.pin1
  N7: MAX485.A, DMX.pin3
  N8: MAX485.B, DMX.pin2
  N9: MAX485.VCC, ESP32.Vin#15

notes:
  ESP32TDMX V1 | made by Luca-Bke
  1    2    3
  +    -

custom parts:
  Mini-360 DC-DC Buck converter: Mini-360 DC-DC Buck converter. Tiny buck step down voltage converter, input voltage 4.75 to 23V output 1 to 17V adjustable. Available from ebay and the like.
  MAX485 Breakout LB Version: MAX485 RS485 breakout board
